// Logisim project e.circ as structural Verilog: 1 circuit, main circuit main
module main (
  input  S,
  input  R,
  output Q,
  output nQ
);

  wire _1_out, _2_out, nor_1_out, nor_2_out;

  nand _1 (_1_out, Q, S);
  nor nor_1 (nor_1_out, _1_out, S, nor_2_out);
  nor nor_2 (nor_2_out, nor_1_out, R, _2_out);
  nand _2 (_2_out, R, nQ);
  not not_1 (Q, nor_1_out);
  not not_2 (nQ, nor_2_out);
endmodule
