// Logisim project r.circ as structural Verilog: 1 circuit, main circuit main
module main (
  input  R,
  input  S,
  output Q,
  output nQ
);

  wire _2_out, not_1_out;

  not not_1 (not_1_out, R);
  nand _2 (_2_out, nQ, S);
  nand _1 (nQ, not_1_out, _2_out);

  assign Q = R;
endmodule
