// Logisim project rs_1.circ as structural Verilog: 1 circuit, main circuit main
module main (
  input  in_1,
  input  in_2,
  output Q,
  output nQ
);

  wire R_out, S_out;

  Button S (.out(S_out));
  Button R (.out(R_out));
  xnor _1 (in_1, in_1, nQ);
  xnor _2 (nQ, in_1, in_1);

  assign in_2 = in_1;
  assign Q = in_1;
endmodule
