// Logisim project rs_2.circ as structural Verilog: 1 circuit, main circuit main
module main (
  input  S,
  input  R,
  output Q,
  output nQ
);

  nand _1 (Q, S, nQ);
  nand _2 (nQ, Q, R);
endmodule
