// Logisim project rs_3.circ as structural Verilog: 1 circuit, main circuit main
module main (
  input  S,
  input  R,
  output Q,
  output nQ
);

  wire and_1_out, and_2_out, \С_out ;

  Clock \u_С  (.out(\С_out ));
  and and_1 (and_1_out, S, \С_out );
  and and_2 (and_2_out, \С_out , R);
  nor nor_1 (Q, and_1_out, nQ);
  nor nor_2 (nQ, Q, and_2_out);
endmodule
