// Logisim project s.circ as structural Verilog: 1 circuit, main circuit main
module main (
  input  S,
  input  R,
  output Q,
  output nQ
);

  wire _2_out, not_1_out;

  not not_1 (not_1_out, S);
  nand _2 (_2_out, nQ, R);
  nand _1 (nQ, not_1_out, _2_out);

  assign Q = S;
endmodule
