// Logisim project t_trig.circ as structural Verilog: 1 circuit, main circuit main
module main (
  input  D,
  output out_2,
  output out_3
);

  wire _1_out, _2_out, _3_out, _4_out, C_out, not_1_out, not_2_out;

  Clock C (.out(C_out));
  not not_1 (not_1_out, C_out);
  not not_2 (not_2_out, C_out);
  nand _1 (_1_out, D, _2_out);
  nand _2 (_2_out, _1_out, not_1_out, C_out);
  nand _3 (_3_out, D, _4_out);
  nand _4 (_4_out, _3_out, C_out, not_2_out);
  nand _5 (out_2, _2_out, out_3);
  nand _6 (out_3, out_2, _4_out);
endmodule
